// Logisim project 实验1-CS2009-U202012656-张锦程.circ as structural Verilog: 5 circuits, main circuit 一位二进制半加器
module \一位二进制半加器  (
  input  A,
  input  B,
  output S,
  output C
);

  wire nand_1_out, nand_2_out, nand_3_out;

  nand nand_1 (nand_1_out, A, B);
  nand nand_2 (nand_2_out, A, nand_1_out);
  nand nand_3 (nand_3_out, nand_1_out, B);
  not not_1 (C, nand_1_out);
  nand nand_4 (S, nand_2_out, nand_3_out);
endmodule

module \一位二进制全加器  (
  input  A,
  input  B,
  input  Ci,
  output S,
  output C0
);

  wire nand_1_out, nand_2_out, xor_1_out;

  xor xor_1 (xor_1_out, A, B);
  nand nand_1 (nand_1_out, xor_1_out, Ci);
  nand nand_2 (nand_2_out, A, B);
  xor xor_2 (S, xor_1_out, Ci);
  nand nand_3 (C0, nand_1_out, nand_2_out);
endmodule

module \串行进位并行加法器  (
  input  A0,
  input  B0,
  input  A1,
  input  B1,
  input  C0,
  input  A2,
  input  A3,
  input  B2,
  input  B3,
  output S0,
  output S1,
  output S2,
  output S3,
  output C4
);

  wire C1_out, C2_out, C3_out, nand_1_out, nand_2_out, nand_3_out, nand_4_out, nand_5_out, nand_6_out,
       nand_7_out, nand_8_out, xor_1_out, xor_3_out, xor_5_out, xor_7_out;

  xor xor_1 (xor_1_out, A0, B0);
  nand nand_1 (nand_1_out, xor_1_out, C0);
  nand nand_2 (nand_2_out, A0, B0);
  xor xor_2 (S0, xor_1_out, C0);
  nand C1 (C1_out, nand_1_out, nand_2_out);
  xor xor_3 (xor_3_out, A1, B1);
  nand nand_3 (nand_3_out, xor_3_out, C1_out);
  nand nand_4 (nand_4_out, A1, B1);
  xor xor_4 (S1, xor_3_out, C1_out);
  nand C2 (C2_out, nand_3_out, nand_4_out);
  xor xor_5 (xor_5_out, A2, B2);
  xor xor_6 (S2, xor_5_out, C2_out);
  nand nand_5 (nand_5_out, xor_5_out, C2_out);
  nand nand_6 (nand_6_out, A2, B2);
  nand C3 (C3_out, nand_5_out, nand_6_out);
  xor xor_7 (xor_7_out, A3, B3);
  nand nand_7 (nand_7_out, xor_7_out, C3_out);
  nand nand_8 (nand_8_out, A3, B3);
  xor xor_8 (S3, xor_7_out, C3_out);
  nand u_C4 (C4, nand_7_out, nand_8_out);
endmodule

module \先行进位并行加法器  (
  input  C0,
  input  A0,
  input  B0,
  input  A1,
  input  B1,
  input  A2,
  input  B2,
  input  A3,
  input  B3,
  output S0,
  output S1,
  output S2,
  output S3,
  output C4
);

  wire and_1_out, and_2_out, and_3_out, and_4_out, and_5_out, and_6_out, and_7_out, and_8_out, and_9_out,
       and_10_out, C1_out, C2_out, C3_out, G0_out, G1_out, G2_out, G3_out, P0_out, P1_out, P2_out, P3_out;

  and G0 (G0_out, A0, B0);
  or P0 (P0_out, A0, B0);
  and G1 (G1_out, A1, B1);
  or P1 (P1_out, A1, B1);
  and G2 (G2_out, A2, B2);
  or P2 (P2_out, A2, B2);
  and G3 (G3_out, A3, B3);
  or P3 (P3_out, A3, B3);
  and and_1 (and_1_out, C0, P0_out);
  and and_2 (and_2_out, P1_out, G0_out);
  and and_3 (and_3_out, C0, P1_out, P0_out);
  and and_4 (and_4_out, P2_out, G1_out);
  and and_5 (and_5_out, P1_out, P2_out, G0_out);
  and and_6 (and_6_out, C0, P2_out, P1_out, P0_out);
  and and_7 (and_7_out, P3_out, G2_out);
  and and_8 (and_8_out, P3_out, P2_out, G1_out);
  and and_9 (and_9_out, P3_out, P2_out, P1_out, G0_out);
  and and_10 (and_10_out, C0, P3_out, P2_out, P1_out, P0_out);
  or C1 (C1_out, G0_out, and_1_out);
  or C2 (C2_out, G1_out, and_2_out, and_3_out);
  or C3 (C3_out, G2_out, and_4_out, and_5_out, and_6_out);
  xor xor_1 (S0, G0_out, P0_out, C0);
  xor xor_2 (S1, P1_out, G1_out, C1_out);
  xor xor_3 (S2, P2_out, G2_out, C2_out);
  xor xor_4 (S3, P3_out, G3_out, C3_out);
  or or_1 (C4, G3_out, and_7_out, and_8_out, and_9_out, and_10_out);
endmodule

module \先行进位并行加法器测试电路  (
  input  in_1,
  input  in_2,
  input  in_3,
  input  in_4,
  input  in_5,
  input  in_6,
  input  in_7,
  input  in_8,
  input  in_9,
  output out_10,
  output out_11,
  output out_12,
  output out_13,
  output out_14
);

  \先行进位并行加法器  \u_先行进位并行加法器_1  (
    .A0(in_5), .B0(in_9), .A1(in_4), .B1(in_8), .A2(in_3), .B2(in_7), .A3(in_2), .B3(in_6), .S0(out_13),
    .S1(out_12), .S2(out_11), .S3(out_10), .C0(in_1), .C4(out_14));
endmodule
