// Logisim project 实验2-CS2009-U202012656-张锦程.circ as structural Verilog: 9 circuits, main circuit 四位二进制可逆计数器
module \四位二进制可逆计数器  (
  input  D,
  input  C,
  input  B,
  input  A,
  input  LD,
  input  CLR,
  input  CPU,
  input  CPD,
  output QD,
  output QC,
  output QB,
  output QA
);

  wire and_1_out, and_2_out, and_3_out, and_4_out, and_5_out, and_6_out, and_7_out, and_8_out, and_9_out,
       and_10_out, buffer_1_out, d_ff_1_qn, d_ff_2_qn, d_ff_3_qn, d_ff_4_qn, or_1_out, or_2_out, or_3_out,
       or_4_out, or_5_out;

  or or_1 (or_1_out, and_1_out, and_3_out);
  and and_1 (and_1_out, CPD, d_ff_4_qn, d_ff_3_qn, d_ff_2_qn);
  and and_2 (and_2_out, D, buffer_1_out);
  and and_3 (and_3_out, CPU, QB, QA, QC);
  D_Flip_Flop #(.trigger("falling"), .Pre_Clr_Positions("ABOVE_BELOW"), .NegatePresetClear("false"), .enable("false"), .NewFFLayout("true")) d_ff_1 (
    .clk(or_1_out), .D(d_ff_1_qn), .Q(QD), .Qn(d_ff_1_qn), .preset(and_2_out), .reset(or_5_out));
  or or_2 (or_2_out, and_5_out, and_4_out);
  and and_4 (and_4_out, CPU, QA, QB);
  and and_5 (and_5_out, CPD, d_ff_4_qn, d_ff_3_qn);
  and and_6 (and_6_out, C, buffer_1_out);
  D_Flip_Flop #(.trigger("falling"), .Pre_Clr_Positions("ABOVE_BELOW"), .NegatePresetClear("false"), .enable("false"), .NewFFLayout("true")) d_ff_2 (
    .clk(or_2_out), .D(d_ff_2_qn), .Q(QC), .Qn(d_ff_2_qn), .preset(and_6_out), .reset(or_5_out));
  and and_7 (and_7_out, CPD, d_ff_4_qn);
  or or_3 (or_3_out, and_7_out, and_8_out);
  and and_8 (and_8_out, CPU, QA);
  and and_9 (and_9_out, B, buffer_1_out);
  D_Flip_Flop #(.trigger("falling"), .Pre_Clr_Positions("ABOVE_BELOW"), .NegatePresetClear("false"), .enable("false"), .NewFFLayout("true")) d_ff_3 (
    .clk(or_3_out), .D(d_ff_3_qn), .Q(QB), .Qn(d_ff_3_qn), .preset(and_9_out), .reset(or_5_out));
  or or_4 (or_4_out, CPD, CPU);
  and and_10 (and_10_out, A, buffer_1_out);
  D_Flip_Flop #(.trigger("falling"), .Pre_Clr_Positions("ABOVE_BELOW"), .NegatePresetClear("false"), .enable("false"), .NewFFLayout("true")) d_ff_4 (
    .clk(or_4_out), .D(d_ff_4_qn), .Q(QA), .Qn(d_ff_4_qn), .preset(and_10_out), .reset(or_5_out));
  buf buffer_1 (buffer_1_out, LD);
  or or_5 (or_5_out, LD, CLR);
endmodule

module \四位二进制可逆计数器测试电路  (
  input  in_1,
  input  in_2,
  input  in_3,
  input  in_4,
  output out_5,
  output out_6,
  output out_7,
  output out_8
);

  wire button_1_out, button_2_out, button_3_out, button_4_out;

  Button button_1 (.out(button_1_out));
  Button button_2 (.out(button_2_out));
  Button button_3 (.out(button_3_out));
  \四位二进制可逆计数器  \u_四位二进制可逆计数器_1  (
    .D(in_1), .C(in_2), .B(in_3), .A(in_4), .QD(out_5), .QC(out_6), .QB(out_7), .QA(out_8),
    .LD(button_4_out), .CPU(button_1_out), .CPD(button_3_out), .CLR(button_2_out));
  Button button_4 (.out(button_4_out));
endmodule

module \二进制转8421码电路  (
  input  B3,
  input  B2,
  input  B1,
  input  B0,
  output out_5,
  output out_6,
  output out_7,
  output out_8,
  output out_9,
  output out_10,
  output out_11,
  output out_12
);

  wire and_1_out, or_1_out;

  \先行进位并行加法器  \u_先行进位并行加法器_1  (
    .A0(B0), .B0(1'b0), .A1(B1), .B1(and_1_out), .A2(B2), .B2(and_1_out), .A3(B3), .B3(1'b0), .S0(out_8),
    .S1(out_7), .S2(out_6), .S3(out_5), .C0(1'b0), .C4(out_9));
  or or_1 (or_1_out, B1, B2);
  and and_1 (and_1_out, B3, or_1_out);

  assign out_10 = 1'b0;
  assign out_11 = 1'b0;
  assign out_12 = 1'b0;
endmodule

module \二进制转8421码测试电路  (
  input  in_1,
  input  in_2,
  input  in_3,
  input  in_4,
  output out_5,
  output out_6,
  output out_7,
  output out_8,
  output out_9,
  output out_10,
  output out_11,
  output out_12
);

  \二进制转8421码电路  \u_二进制转8421码电路_1  (
    .out_5(out_9), .out_6(out_10), .out_7(out_11), .out_8(out_12), .out_9(out_8), .out_10(out_7),
    .out_11(out_6), .out_12(out_5), .B3(in_1), .B2(in_2), .B1(in_3), .B0(in_4));
endmodule

module \显示电路  (
  input  in_1,
  input  in_2,
  input  in_3,
  input  in_4,
  output out_5,
  output out_6,
  output out_7,
  output out_8,
  output out_9,
  output out_10,
  output out_11
);

  wire and_1_out, and_2_out, and_3_out, and_4_out, and_5_out, and_6_out, and_7_out, and_8_out, and_9_out,
       and_10_out, and_11_out, and_12_out, and_13_out, and_14_out, and_15_out, and_16_out, and_17_out,
       and_18_out, and_19_out, and_20_out, and_21_out, not_1_out, not_2_out, not_3_out, not_4_out;

  not not_1 (not_1_out, in_1);
  not not_2 (not_2_out, in_2);
  not not_3 (not_3_out, in_3);
  not not_4 (not_4_out, in_4);
  and and_1 (and_1_out, not_2_out, not_3_out, not_4_out);
  and and_2 (and_2_out, not_1_out, not_2_out, in_3);
  and and_3 (and_3_out, not_1_out, in_2, in_4);
  and and_4 (and_4_out, in_1, not_3_out, in_4);
  and and_5 (and_5_out, not_1_out, in_3, in_4);
  and and_6 (and_6_out, not_1_out, not_2_out);
  and and_7 (and_7_out, not_3_out, not_4_out);
  and and_8 (and_8_out, not_2_out, not_3_out);
  and and_9 (and_9_out, not_1_out, in_2);
  and and_10 (and_10_out, not_2_out, in_4);
  and and_11 (and_11_out, not_2_out, not_4_out);
  and and_12 (and_12_out, in_2, not_3_out, in_4);
  and and_13 (and_13_out, not_2_out, in_3, in_4);
  and and_14 (and_14_out, in_2, in_3, not_4_out);
  and and_15 (and_15_out, in_3, not_4_out);
  and and_16 (and_16_out, not_3_out, not_4_out);
  and and_17 (and_17_out, in_2, not_3_out);
  and and_18 (and_18_out, in_2, not_4_out);
  and and_19 (and_19_out, in_1, not_2_out, not_3_out);
  and and_20 (and_20_out, in_1, not_2_out);
  and and_21 (and_21_out, not_2_out, in_3);
  or or_1 (out_6, and_5_out, and_6_out, and_7_out, and_8_out);
  or or_2 (out_7, and_8_out, and_9_out, and_10_out);
  or or_3 (out_8, and_11_out, and_12_out, and_13_out, and_14_out);
  or or_4 (out_11, and_15_out, and_17_out, and_20_out, and_21_out);
  or or_5 (out_5, and_1_out, and_2_out, and_3_out, and_4_out);
  or or_6 (out_9, and_11_out, and_15_out);
  or or_7 (out_10, and_16_out, and_17_out, and_18_out, and_19_out);
endmodule

module \显示电路测试电路  (
  input  in_1,
  input  in_2,
  input  in_3,
  input  in_4
);

  wire \二进制转8421码电路_1_out_5 , \二进制转8421码电路_1_out_6 , \二进制转8421码电路_1_out_7 , \二进制转8421码电路_1_out_8 ,
       \二进制转8421码电路_1_out_9 , \二进制转8421码电路_1_out_10 , \二进制转8421码电路_1_out_11 , \二进制转8421码电路_1_out_12 ,
       \显示电路_1_out_5 , \显示电路_1_out_6 , \显示电路_1_out_7 , \显示电路_1_out_8 , \显示电路_1_out_9 , \显示电路_1_out_10 ,
       \显示电路_1_out_11 , \显示电路_2_out_5 , \显示电路_2_out_6 , \显示电路_2_out_7 , \显示电路_2_out_8 , \显示电路_2_out_9 ,
       \显示电路_2_out_10 , \显示电路_2_out_11 ;

  \显示电路  \u_显示电路_1  (
    .in_1(\二进制转8421码电路_1_out_12 ), .in_2(\二进制转8421码电路_1_out_11 ), .in_3(\二进制转8421码电路_1_out_10 ),
    .in_4(\二进制转8421码电路_1_out_9 ), .out_5(\显示电路_1_out_5 ), .out_6(\显示电路_1_out_6 ), .out_7(\显示电路_1_out_7 ),
    .out_8(\显示电路_1_out_8 ), .out_9(\显示电路_1_out_9 ), .out_10(\显示电路_1_out_10 ), .out_11(\显示电路_1_out_11 ));
  _7_Segment_Display #(.active("true")) u_7_segment_display_1 (
    .g(\显示电路_1_out_11 ), .f(\显示电路_1_out_10 ), .a(\显示电路_1_out_5 ), .b(\显示电路_1_out_6 ), .e(\显示电路_1_out_9 ),
    .d(\显示电路_1_out_8 ), .c(\显示电路_1_out_7 ));  // open: dp
  \显示电路  \u_显示电路_2  (
    .in_1(\二进制转8421码电路_1_out_5 ), .in_2(\二进制转8421码电路_1_out_6 ), .in_3(\二进制转8421码电路_1_out_7 ),
    .in_4(\二进制转8421码电路_1_out_8 ), .out_5(\显示电路_2_out_5 ), .out_6(\显示电路_2_out_6 ), .out_7(\显示电路_2_out_7 ),
    .out_8(\显示电路_2_out_8 ), .out_9(\显示电路_2_out_9 ), .out_10(\显示电路_2_out_10 ), .out_11(\显示电路_2_out_11 ));
  \二进制转8421码电路  \u_二进制转8421码电路_1  (
    .out_5(\二进制转8421码电路_1_out_5 ), .out_6(\二进制转8421码电路_1_out_6 ), .out_7(\二进制转8421码电路_1_out_7 ),
    .out_8(\二进制转8421码电路_1_out_8 ), .out_9(\二进制转8421码电路_1_out_9 ), .out_10(\二进制转8421码电路_1_out_10 ),
    .out_11(\二进制转8421码电路_1_out_11 ), .out_12(\二进制转8421码电路_1_out_12 ), .B3(in_1), .B2(in_2), .B1(in_3),
    .B0(in_4));
  _7_Segment_Display #(.active("true")) u_7_segment_display_2 (
    .g(\显示电路_2_out_11 ), .f(\显示电路_2_out_10 ), .a(\显示电路_2_out_5 ), .b(\显示电路_2_out_6 ), .e(\显示电路_2_out_9 ),
    .d(\显示电路_2_out_8 ), .c(\显示电路_2_out_7 ));  // open: dp
endmodule

module \报警电路  (
  input  U,
  input  CLR,
  input  D,
  input  in_4,
  input  in_5,
  input  in_6,
  input  in_7,
  input  in_8,
  output out_9,
  output out_10,
  output out_11,
  output out_12
);

  wire and_1_out, and_2_out, and_3_out, not_1_out, \无人_out , \满员_out ;

  LED #(.active("true")) \u_报警灯  (.in(and_1_out));
  and and_1 (and_1_out, U, \满员_out );
  not not_1 (not_1_out, \满员_out );
  and and_2 (and_2_out, not_1_out, U);
  and and_3 (and_3_out, \无人_out , D);
  or \u_无人  (\无人_out , out_12, out_11, out_10, out_9);
  and \u_满员  (\满员_out , out_12, out_11, out_10, out_9);
  \四位二进制可逆计数器  \u_四位二进制可逆计数器_1  (
    .D(in_4), .C(in_5), .B(in_6), .A(in_7), .QD(out_9), .QC(out_10), .QB(out_11), .QA(out_12), .LD(in_8),
    .CPU(and_2_out), .CPD(and_3_out), .CLR(CLR));
endmodule

module \小型实验室门禁系统  (
  input  U,
  input  CLR,
  input  D,
  output out_4,
  output out_5,
  output out_6,
  output out_7,
  output out_8,
  output out_9,
  output out_10,
  output out_11,
  output out_12,
  output out_13,
  output out_14,
  output out_15,
  output out_16,
  output out_17,
  output out_18
);

  wire and_2_out, and_3_out, not_1_out, \二进制转8421码电路_1_out_5 , \二进制转8421码电路_1_out_6 , \二进制转8421码电路_1_out_7 ,
       \二进制转8421码电路_1_out_8 , \二进制转8421码电路_1_out_9 , \二进制转8421码电路_1_out_10 , \二进制转8421码电路_1_out_11 ,
       \二进制转8421码电路_1_out_12 , \四位二进制可逆计数器_1_qa , \四位二进制可逆计数器_1_qb , \四位二进制可逆计数器_1_qc , \四位二进制可逆计数器_1_qd ,
       \无人_out , \满员_out ;

  and and_1 (out_18, U, \满员_out );
  \显示电路  \u_显示电路_1  (
    .in_1(\二进制转8421码电路_1_out_12 ), .in_2(\二进制转8421码电路_1_out_11 ), .in_3(\二进制转8421码电路_1_out_10 ),
    .in_4(\二进制转8421码电路_1_out_9 ), .out_5(out_4), .out_6(out_5), .out_7(out_6), .out_8(out_7), .out_9(out_8),
    .out_10(out_9), .out_11(out_10));
  not not_1 (not_1_out, \满员_out );
  and and_2 (and_2_out, not_1_out, U);
  and and_3 (and_3_out, \无人_out , D);
  or \u_无人  (\无人_out , \四位二进制可逆计数器_1_qa , \四位二进制可逆计数器_1_qb , \四位二进制可逆计数器_1_qc , \四位二进制可逆计数器_1_qd );
  and \u_满员  (\满员_out , \四位二进制可逆计数器_1_qa , \四位二进制可逆计数器_1_qb , \四位二进制可逆计数器_1_qc , \四位二进制可逆计数器_1_qd );
  \显示电路  \u_显示电路_2  (
    .in_1(\二进制转8421码电路_1_out_5 ), .in_2(\二进制转8421码电路_1_out_6 ), .in_3(\二进制转8421码电路_1_out_7 ),
    .in_4(\二进制转8421码电路_1_out_8 ), .out_5(out_11), .out_6(out_12), .out_7(out_13), .out_8(out_14),
    .out_9(out_15), .out_10(out_16), .out_11(out_17));
  \二进制转8421码电路  \u_二进制转8421码电路_1  (
    .out_5(\二进制转8421码电路_1_out_5 ), .out_6(\二进制转8421码电路_1_out_6 ), .out_7(\二进制转8421码电路_1_out_7 ),
    .out_8(\二进制转8421码电路_1_out_8 ), .out_9(\二进制转8421码电路_1_out_9 ), .out_10(\二进制转8421码电路_1_out_10 ),
    .out_11(\二进制转8421码电路_1_out_11 ), .out_12(\二进制转8421码电路_1_out_12 ), .B3(\四位二进制可逆计数器_1_qd ),
    .B2(\四位二进制可逆计数器_1_qc ), .B1(\四位二进制可逆计数器_1_qb ), .B0(\四位二进制可逆计数器_1_qa ));
  \四位二进制可逆计数器  \u_四位二进制可逆计数器_1  (
    .D(1'b0), .C(1'b0), .B(1'b0), .A(1'b0), .QD(\四位二进制可逆计数器_1_qd ), .QC(\四位二进制可逆计数器_1_qc ),
    .QB(\四位二进制可逆计数器_1_qb ), .QA(\四位二进制可逆计数器_1_qa ), .LD(1'b0), .CPU(and_2_out), .CPD(and_3_out), .CLR(CLR));
endmodule

module \小型门禁系统测试电路  (
);

  wire button_1_out, button_2_out, button_3_out, \小型实验室门禁系统_1_out_4 , \小型实验室门禁系统_1_out_5 ,
       \小型实验室门禁系统_1_out_6 , \小型实验室门禁系统_1_out_7 , \小型实验室门禁系统_1_out_8 , \小型实验室门禁系统_1_out_9 ,
       \小型实验室门禁系统_1_out_10 , \小型实验室门禁系统_1_out_11 , \小型实验室门禁系统_1_out_12 , \小型实验室门禁系统_1_out_13 ,
       \小型实验室门禁系统_1_out_14 , \小型实验室门禁系统_1_out_15 , \小型实验室门禁系统_1_out_16 , \小型实验室门禁系统_1_out_17 ,
       \小型实验室门禁系统_1_out_18 ;

  Button button_1 (.out(button_1_out));
  Button button_2 (.out(button_2_out));
  Button button_3 (.out(button_3_out));
  _7_Segment_Display #(.active("true")) u_7_segment_display_1 (
    .g(\小型实验室门禁系统_1_out_10 ), .f(\小型实验室门禁系统_1_out_9 ), .a(\小型实验室门禁系统_1_out_4 ), .b(\小型实验室门禁系统_1_out_5 ),
    .e(\小型实验室门禁系统_1_out_8 ), .d(\小型实验室门禁系统_1_out_7 ), .c(\小型实验室门禁系统_1_out_6 ));  // open: dp
  _7_Segment_Display #(.active("true")) u_7_segment_display_2 (
    .g(\小型实验室门禁系统_1_out_17 ), .f(\小型实验室门禁系统_1_out_16 ), .a(\小型实验室门禁系统_1_out_11 ), .b(\小型实验室门禁系统_1_out_12 ),
    .e(\小型实验室门禁系统_1_out_15 ), .d(\小型实验室门禁系统_1_out_14 ), .c(\小型实验室门禁系统_1_out_13 ));  // open: dp
  \小型实验室门禁系统  \u_小型实验室门禁系统_1  (
    .U(button_1_out), .CLR(button_2_out), .D(button_3_out), .out_18(\小型实验室门禁系统_1_out_18 ),
    .out_4(\小型实验室门禁系统_1_out_4 ), .out_5(\小型实验室门禁系统_1_out_5 ), .out_6(\小型实验室门禁系统_1_out_6 ),
    .out_7(\小型实验室门禁系统_1_out_7 ), .out_8(\小型实验室门禁系统_1_out_8 ), .out_9(\小型实验室门禁系统_1_out_9 ),
    .out_10(\小型实验室门禁系统_1_out_10 ), .out_11(\小型实验室门禁系统_1_out_11 ), .out_12(\小型实验室门禁系统_1_out_12 ),
    .out_13(\小型实验室门禁系统_1_out_13 ), .out_14(\小型实验室门禁系统_1_out_14 ), .out_15(\小型实验室门禁系统_1_out_15 ),
    .out_16(\小型实验室门禁系统_1_out_16 ), .out_17(\小型实验室门禁系统_1_out_17 ));
  LED #(.active("true")) led_1 (.in(\小型实验室门禁系统_1_out_18 ));
endmodule
