// Logisim project 实验5-CS2009-U202012656-张锦程.circ as structural Verilog: 15 circuits, main circuit 四位二进制可逆计数器
module \四位二进制可逆计数器  (
  input  in_1,
  input  in_2,
  input  in_3,
  input  in_4,
  input  LD,
  input  CLR,
  input  CPU,
  input  CPD,
  output QD,
  output QC,
  output QB,
  output QA
);

  wire and_1_out, and_2_out, and_3_out, and_4_out, and_5_out, and_6_out, and_7_out, and_8_out, and_9_out,
       and_10_out, buffer_1_out, d_ff_1_qn, d_ff_2_qn, d_ff_3_qn, d_ff_4_qn, or_1_out, or_2_out, or_3_out,
       or_4_out, or_5_out;

  or or_1 (or_1_out, and_1_out, and_2_out);
  and and_1 (and_1_out, CPD, d_ff_4_qn, d_ff_3_qn, d_ff_2_qn);
  and and_2 (and_2_out, CPU, QB, QA, QC);
  and and_3 (and_3_out, in_1, buffer_1_out);
  D_Flip_Flop #(.trigger("falling"), .Pre_Clr_Positions("ABOVE_BELOW"), .NegatePresetClear("false"), .enable("false"), .NewFFLayout("true")) d_ff_1 (
    .clk(or_1_out), .D(d_ff_1_qn), .Q(QD), .Qn(d_ff_1_qn), .preset(and_3_out), .reset(or_5_out));
  or or_2 (or_2_out, and_4_out, and_5_out);
  and and_4 (and_4_out, CPD, d_ff_4_qn, d_ff_3_qn);
  and and_5 (and_5_out, CPU, QA, QB);
  and and_6 (and_6_out, in_2, buffer_1_out);
  D_Flip_Flop #(.trigger("falling"), .Pre_Clr_Positions("ABOVE_BELOW"), .NegatePresetClear("false"), .enable("false"), .NewFFLayout("true")) d_ff_2 (
    .clk(or_2_out), .D(d_ff_2_qn), .Q(QC), .Qn(d_ff_2_qn), .preset(and_6_out), .reset(or_5_out));
  or or_3 (or_3_out, and_7_out, and_8_out);
  and and_7 (and_7_out, CPD, d_ff_4_qn);
  and and_8 (and_8_out, CPU, QA);
  and and_9 (and_9_out, in_3, buffer_1_out);
  D_Flip_Flop #(.trigger("falling"), .Pre_Clr_Positions("ABOVE_BELOW"), .NegatePresetClear("false"), .enable("false"), .NewFFLayout("true")) d_ff_3 (
    .clk(or_3_out), .D(d_ff_3_qn), .Q(QB), .Qn(d_ff_3_qn), .preset(and_9_out), .reset(or_5_out));
  or or_4 (or_4_out, CPD, CPU);
  and and_10 (and_10_out, in_4, buffer_1_out);
  D_Flip_Flop #(.trigger("falling"), .Pre_Clr_Positions("ABOVE_BELOW"), .NegatePresetClear("false"), .enable("false"), .NewFFLayout("true")) d_ff_4 (
    .clk(or_4_out), .D(d_ff_4_qn), .Q(QA), .Qn(d_ff_4_qn), .preset(and_10_out), .reset(or_5_out));
  buf buffer_1 (buffer_1_out, LD);
  or or_5 (or_5_out, LD, CLR);
endmodule

module \六十进制计数器  (
  input  cir,
  input  cpu,
  input  cpd,
  input  adj,
  output out_5,
  output out_6,
  output out_7,
  output out_8,
  output out_9,
  output out_10,
  output out_11,
  output out_12,
  output out_13
);

  wire and_1_out, and_2_out, and_3_out, and_4_out, and_5_out, and_6_out, buffer_1_out, d_ff_1_q, d_ff_1_qn,
       not_1_out, not_2_out, or_1_out, or_2_out, or_3_out, or_4_out;

  not not_1 (not_1_out, adj);
  and and_1 (and_1_out, cpd, adj);
  D_Flip_Flop #(.trigger("rising"), .Pre_Clr_Positions("ABOVE_BELOW"), .NegatePresetClear("false"), .enable("false"), .NewFFLayout("true")) d_ff_1 (
    .clk(not_1_out), .D(d_ff_1_qn), .Q(d_ff_1_q), .Qn(d_ff_1_qn));  // open: preset, reset
  and and_2 (and_2_out, out_9, out_11);
  or or_1 (or_1_out, buffer_1_out, and_2_out, cir);
  or or_2 (or_2_out, out_9, out_10, out_11, out_12);
  and and_3 (and_3_out, or_2_out, and_1_out);
  not not_2 (not_2_out, d_ff_1_q);
  and and_4 (and_4_out, not_2_out, and_1_out);
  \四位二进制可逆计数器  \u_四位二进制可逆计数器_1  (
    .in_1(1'b0), .in_2(1'b0), .in_3(1'b0), .in_4(1'b0), .LD(1'b0), .QD(out_9), .QC(out_10), .QB(out_11),
    .QA(out_12), .CLR(or_1_out), .CPU(cpu), .CPD(and_3_out));
  and and_5 (and_5_out, cpu, out_9, out_10, out_11, out_12);
  or or_3 (or_3_out, and_2_out, and_5_out);
  or or_4 (or_4_out, cir, buffer_1_out);
  and and_6 (and_6_out, out_7, out_6);
  buf buffer_1 (buffer_1_out, and_6_out);
  \四位二进制可逆计数器  \u_四位二进制可逆计数器_2  (
    .in_1(1'b0), .in_2(1'b0), .in_3(1'b0), .in_4(1'b0), .LD(1'b0), .QD(out_5), .QC(out_6), .QB(out_7),
    .QA(out_8), .CLR(or_4_out), .CPU(or_3_out), .CPD(and_4_out));
  and and_7 (out_13, and_6_out, not_1_out);
endmodule

module \六十进制计数器测试电路  (
  input  in_1,
  input  in_2,
  input  in_3,
  output out_4
);

  wire clock_1_out, d_ff_1_qn, \六十进制计数器_1_out_13 ;
  wire [3:0] \六十进制计数器_1_out_8 , \六十进制计数器_1_out_12 ;

  Clock #(.highDuration(1), .lowDuration(5)) clock_1 (.out(clock_1_out));
  Hex_Digit_Display hex_digit_display_1 (.value(\六十进制计数器_1_out_8 ));  // open: dp
  Hex_Digit_Display hex_digit_display_2 (.value(\六十进制计数器_1_out_12 ));  // open: dp
  \六十进制计数器  \u_六十进制计数器_1  (
    .cir(in_3), .cpu(clock_1_out), .cpd(in_2), .adj(in_1), .out_9(\六十进制计数器_1_out_12 [3]),
    .out_10(\六十进制计数器_1_out_12 [2]), .out_11(\六十进制计数器_1_out_12 [1]), .out_12(\六十进制计数器_1_out_12 [0]),
    .out_5(\六十进制计数器_1_out_8 [3]), .out_6(\六十进制计数器_1_out_8 [2]), .out_7(\六十进制计数器_1_out_8 [1]),
    .out_8(\六十进制计数器_1_out_8 [0]), .out_13(\六十进制计数器_1_out_13 ));
  D_Flip_Flop #(.trigger("rising"), .Pre_Clr_Positions("ABOVE_BELOW"), .NegatePresetClear("false"), .enable("false"), .NewFFLayout("true")) d_ff_1 (
    .clk(\六十进制计数器_1_out_13 ), .D(d_ff_1_qn), .Q(out_4), .Qn(d_ff_1_qn));  // open: preset, reset
endmodule

module \十二进制计数器或二十四进制的计数器电路  (
  input  in_1,
  input  cir,
  input  cpu,
  input  cpd,
  input  adj,
  output out_6,
  output out_7,
  output out_8,
  output out_9,
  output out_10,
  output out_11,
  output out_12,
  output out_13,
  output out_14
);

  wire and_1_out, and_2_out, and_3_out, and_4_out, and_5_out, and_6_out, and_7_out, and_8_out, and_9_out,
       and_10_out, d_ff_1_q, d_ff_1_qn, not_1_out, not_2_out, not_3_out, or_1_out, or_2_out, or_3_out,
       or_4_out, or_5_out, or_6_out;

  not not_1 (not_1_out, adj);
  and and_1 (and_1_out, cpd, adj);
  D_Flip_Flop #(.trigger("rising"), .Pre_Clr_Positions("ABOVE_BELOW"), .NegatePresetClear("false"), .enable("false"), .NewFFLayout("true")) d_ff_1 (
    .clk(not_1_out), .D(d_ff_1_qn), .Q(d_ff_1_q), .Qn(d_ff_1_qn));  // open: preset, reset
  and and_2 (and_2_out, out_10, out_12);
  or or_1 (or_1_out, or_6_out, and_2_out, cir);
  and and_3 (and_3_out, and_1_out, or_2_out);
  or or_2 (or_2_out, out_10, out_11, out_12, out_13);
  not not_2 (not_2_out, d_ff_1_q);
  and and_4 (and_4_out, not_2_out, and_1_out);
  \四位二进制可逆计数器  \u_四位二进制可逆计数器_1  (
    .in_1(1'b0), .in_2(1'b0), .in_3(1'b0), .in_4(1'b0), .LD(1'b0), .QD(out_10), .QC(out_11), .QB(out_12),
    .QA(out_13), .CLR(or_1_out), .CPU(cpu), .CPD(and_3_out));
  and and_5 (and_5_out, cpu, out_10, out_11, out_12, out_13);
  or or_3 (or_3_out, out_6, out_7, out_9, out_8);
  or or_4 (or_4_out, and_2_out, and_5_out);
  and and_6 (and_6_out, and_4_out, or_3_out);
  and and_7 (and_7_out, out_8, out_11);
  and and_8 (and_8_out, out_9, out_12);
  \四位二进制可逆计数器  \u_四位二进制可逆计数器_2  (
    .in_1(1'b0), .in_2(1'b0), .in_3(1'b0), .in_4(1'b0), .LD(1'b0), .QD(out_6), .QC(out_7), .QB(out_8),
    .QA(out_9), .CLR(or_5_out), .CPU(or_4_out), .CPD(and_6_out));
  and and_9 (and_9_out, and_7_out, in_1);
  not not_3 (not_3_out, in_1);
  and and_10 (and_10_out, not_3_out, and_8_out);
  or or_5 (or_5_out, cir, or_6_out);
  or or_6 (or_6_out, and_9_out, and_10_out);
  and and_11 (out_14, or_6_out, not_1_out);
endmodule

module \十二进制计数器或二十四进制的计数器测试电路  (
  input  in_1,
  input  in_2,
  input  in_3,
  input  in_4,
  output out_5
);

  wire clock_1_out, d_ff_1_qn, \十二进制计数器或二十四进制的计数器电路_1_out_14 ;
  wire [3:0] \十二进制计数器或二十四进制的计数器电路_1_out_9 , \十二进制计数器或二十四进制的计数器电路_1_out_13 ;

  Clock #(.highDuration(10), .lowDuration(10)) clock_1 (.out(clock_1_out));
  Hex_Digit_Display hex_digit_display_1 (.value(\十二进制计数器或二十四进制的计数器电路_1_out_9 ));  // open: dp
  Hex_Digit_Display hex_digit_display_2 (.value(\十二进制计数器或二十四进制的计数器电路_1_out_13 ));  // open: dp
  \十二进制计数器或二十四进制的计数器电路  \u_十二进制计数器或二十四进制的计数器电路_1  (
    .in_1(in_2), .cir(in_4), .cpu(clock_1_out), .cpd(in_3), .adj(in_1),
    .out_10(\十二进制计数器或二十四进制的计数器电路_1_out_13 [3]), .out_11(\十二进制计数器或二十四进制的计数器电路_1_out_13 [2]),
    .out_12(\十二进制计数器或二十四进制的计数器电路_1_out_13 [1]), .out_13(\十二进制计数器或二十四进制的计数器电路_1_out_13 [0]),
    .out_6(\十二进制计数器或二十四进制的计数器电路_1_out_9 [3]), .out_7(\十二进制计数器或二十四进制的计数器电路_1_out_9 [2]),
    .out_8(\十二进制计数器或二十四进制的计数器电路_1_out_9 [1]), .out_9(\十二进制计数器或二十四进制的计数器电路_1_out_9 [0]),
    .out_14(\十二进制计数器或二十四进制的计数器电路_1_out_14 ));
  D_Flip_Flop #(.trigger("rising"), .Pre_Clr_Positions("ABOVE_BELOW"), .NegatePresetClear("false"), .enable("false"), .NewFFLayout("true")) d_ff_1 (
    .clk(\十二进制计数器或二十四进制的计数器电路_1_out_14 ), .D(d_ff_1_qn), .Q(out_5), .Qn(d_ff_1_qn));  // open: preset, reset
endmodule

module \上下午文字显示的电路  (
  input  in_1,
  input  in_2,
  output [6:0] out_3,
  output [6:0] out_4,
  output [6:0] out_5,
  output [6:0] out_6,
  output [6:0] out_7
);

  wire not_1_out, not_2_out, not_3_out, not_4_out, not_5_out, not_6_out;
  wire [6:0] controlled_buffer_1_out, controlled_buffer_3_out, controlled_buffer_5_out,
       controlled_buffer_7_out, controlled_buffer_9_out;

  assign controlled_buffer_1_out = not_2_out ? 7'b0000001 : 7'bz;  // Controlled_Buffer controlled_buffer_1
  not not_1 (not_1_out, not_2_out);
  not not_2 (not_2_out, in_2);
  assign controlled_buffer_1_out = not_1_out ? 7'b1000000 : 7'bz;  // Controlled_Buffer controlled_buffer_2
  assign controlled_buffer_3_out = not_2_out ? 7'b0000001 : 7'bz;  // Controlled_Buffer controlled_buffer_3
  not not_3 (not_3_out, not_2_out);
  assign controlled_buffer_3_out = not_3_out ? 7'b1000000 : 7'bz;  // Controlled_Buffer controlled_buffer_4
  assign controlled_buffer_5_out = not_2_out ? {7{1'b1}} : 7'bz;  // Controlled_Buffer controlled_buffer_5
  not not_4 (not_4_out, not_2_out);
  assign controlled_buffer_5_out = not_4_out ? {7{1'b1}} : 7'bz;  // Controlled_Buffer controlled_buffer_6
  assign controlled_buffer_7_out = not_2_out ? 7'b0001001 : 7'bz;  // Controlled_Buffer controlled_buffer_7
  not not_5 (not_5_out, not_2_out);
  assign controlled_buffer_7_out = not_5_out ? 7'b1001000 : 7'bz;  // Controlled_Buffer controlled_buffer_8
  assign controlled_buffer_9_out = not_2_out ? 7'b0001001 : 7'bz;  // Controlled_Buffer controlled_buffer_9
  not not_6 (not_6_out, not_2_out);
  assign controlled_buffer_9_out = not_6_out ? 7'b1001000 : 7'bz;  // Controlled_Buffer controlled_buffer_10
  assign out_3 = in_1 ? controlled_buffer_1_out : 7'bz;  // Controlled_Buffer controlled_buffer_11
  assign out_4 = in_1 ? controlled_buffer_3_out : 7'bz;  // Controlled_Buffer controlled_buffer_12
  assign out_5 = in_1 ? controlled_buffer_5_out : 7'bz;  // Controlled_Buffer controlled_buffer_13
  assign out_6 = in_1 ? controlled_buffer_7_out : 7'bz;  // Controlled_Buffer controlled_buffer_14
  assign out_7 = in_1 ? controlled_buffer_9_out : 7'bz;  // Controlled_Buffer controlled_buffer_15
endmodule

module \上下午文字显示测试电路  (
  input  in_1,
  input  in_2
);

  wire [6:0] \上下午文字显示的电路_1_out_3 , \上下午文字显示的电路_1_out_4 , \上下午文字显示的电路_1_out_5 , \上下午文字显示的电路_1_out_6 ,
       \上下午文字显示的电路_1_out_7 ;

  DotMatrix #(.inputtype("column"), .matrixcols(5), .matrixrows(7), .persist(0), .dotshape("square")) dotmatrix_1 (
    .col0(\上下午文字显示的电路_1_out_3 ), .col1(\上下午文字显示的电路_1_out_4 ), .col2(\上下午文字显示的电路_1_out_5 ),
    .col3(\上下午文字显示的电路_1_out_6 ), .col4(\上下午文字显示的电路_1_out_7 ));
  \上下午文字显示的电路  \u_上下午文字显示的电路_1  (
    .in_1(in_2), .out_3(\上下午文字显示的电路_1_out_3 ), .out_4(\上下午文字显示的电路_1_out_4 ), .out_5(\上下午文字显示的电路_1_out_5 ),
    .out_6(\上下午文字显示的电路_1_out_6 ), .out_7(\上下午文字显示的电路_1_out_7 ), .in_2(in_1));
endmodule

module \电子钟整点报时电路  (
  input  [23:0] in_1,
  input  [23:0] in_2,
  input  in_3,
  output out_4
);

  wire [23:0] register_1_q, xnor_1_out;

  Register #(.width(24), .trigger("rising"), .Select("low")) register_1 (
    .D(in_1), .Q(register_1_q), .clk(in_3));  // open: en, clr
  assign xnor_1_out = ~(register_1_q ^ in_2);  // XNOR_Gate xnor_1, 24 bits wide
  and and_1 (out_4, xnor_1_out[0], xnor_1_out[1], xnor_1_out[2], xnor_1_out[3], xnor_1_out[4], xnor_1_out[5], xnor_1_out[6], xnor_1_out[7], xnor_1_out[8], xnor_1_out[9], xnor_1_out[10], xnor_1_out[11], xnor_1_out[12], xnor_1_out[13], xnor_1_out[14], xnor_1_out[15], xnor_1_out[16], xnor_1_out[17], xnor_1_out[18], xnor_1_out[19], xnor_1_out[20], xnor_1_out[21], xnor_1_out[22], xnor_1_out[23]);
endmodule

module \电子钟整点报时电路测试电路  (
  input  in_1,
  input  [23:0] in_2,
  input  [23:0] in_3,
  output out_4
);

  \电子钟整点报时电路  \u_电子钟整点报时电路_1  (.out_4(out_4), .in_1(in_2), .in_2(in_3), .in_3(in_1));
endmodule

module \秒脉冲产生电路  (
  input  in_1,
  output out_2
);

  wire d_ff_1_q, d_ff_1_qn, d_ff_2_q, d_ff_2_qn, d_ff_3_qn;

  D_Flip_Flop #(.trigger("rising"), .Pre_Clr_Positions("ABOVE_BELOW"), .NegatePresetClear("false"), .enable("false"), .NewFFLayout("true")) d_ff_1 (
    .clk(in_1), .D(d_ff_1_qn), .Q(d_ff_1_q), .Qn(d_ff_1_qn));  // open: preset, reset
  D_Flip_Flop #(.trigger("rising"), .Pre_Clr_Positions("ABOVE_BELOW"), .NegatePresetClear("false"), .enable("false"), .NewFFLayout("true")) d_ff_2 (
    .clk(d_ff_1_q), .D(d_ff_2_qn), .Q(d_ff_2_q), .Qn(d_ff_2_qn));  // open: preset, reset
  D_Flip_Flop #(.trigger("rising"), .Pre_Clr_Positions("ABOVE_BELOW"), .NegatePresetClear("false"), .enable("false"), .NewFFLayout("true")) d_ff_3 (
    .clk(d_ff_2_q), .D(d_ff_3_qn), .Q(out_2), .Qn(d_ff_3_qn));  // open: preset, reset
endmodule

module \秒脉冲产生电路测试电路  (
);

  wire clock_1_out, \秒脉冲产生电路_1_out_2 ;

  Clock #(.highDuration(10), .lowDuration(10)) clock_1 (.out(clock_1_out));
  \秒脉冲产生电路  \u_秒脉冲产生电路_1  (.in_1(clock_1_out), .out_2(\秒脉冲产生电路_1_out_2 ));
  LED #(.active("true")) led_1 (.in(\秒脉冲产生电路_1_out_2 ));
endmodule

module \多功能数字钟  (
  input  CP,
  input  set,
  input  clr,
  input  adj0,
  input  adj1,
  input  cpd,
  input  cpu,
  output out_8,
  output [6:0] out_9,
  output [6:0] out_10,
  output out_11,
  output out_12,
  output out_13,
  output out_14,
  output out_15,
  output out_16,
  output out_17,
  output out_18,
  output out_19,
  output out_20,
  output out_21,
  output out_22,
  output out_23,
  output out_24,
  output out_25,
  output out_26,
  output [6:0] out_27,
  output [6:0] out_28,
  output out_29,
  output out_30,
  output out_31,
  output out_32,
  output out_33,
  output out_34,
  output out_35,
  output out_36,
  output [6:0] out_37,
  output out_38
);

  wire and_1_out, and_2_out, and_3_out, and_4_out, and_5_out, and_6_out, and_7_out, and_8_out, clock_1_out,
       d_ff_1_q, d_ff_1_qn, not_1_out, not_2_out, or_1_out, or_2_out, or_3_out, or_4_out, or_5_out, or_6_out,
       \分钟_out_13 , \十二进制计数器或二十四进制的计数器电路_1_out_14 , \秒脉冲产生电路_1_out_2 , \秒钟_out_13 ;
  wire [23:0] multiplexer_1_out;

  Clock #(.highDuration(1), .lowDuration(1)) clock_1 (.out(clock_1_out));
  \秒脉冲产生电路  \u_秒脉冲产生电路_1  (.in_1(CP), .out_2(\秒脉冲产生电路_1_out_2 ));
  \闹钟  \u_闹钟_1  (
    .in_2(4'b0000), .in_3(4'b0000), .in_4(4'b0000), .in_5(4'b0000), .in_6(4'b0001), .in_7(4'b0000), .CP(CP),
    .adj0(adj0), .adj1(adj1), .cpd(cpd), .cpu(cpu), .set(set), .clr(clr), .in_1(1'b1), .out_15(out_38));  // open: out_16, out_17, out_18, out_19, out_20, out_21, out_22, out_23, out_24, out_25, out_26, out_27, out_28, out_29, out_30, out_31, out_32, out_33, out_34, out_35, out_36, out_37, out_38, out_39
  \六十进制计数器  \u_秒钟  (
    .cir(clr), .cpu(\秒脉冲产生电路_1_out_2 ), .cpd(1'b0), .adj(adj0), .out_9(out_15), .out_10(out_16),
    .out_11(out_17), .out_12(out_18), .out_5(out_11), .out_6(out_12), .out_7(out_13), .out_8(out_14),
    .out_13(\秒钟_out_13 ));
  and and_1 (and_1_out, adj0, adj1, cpu);
  or or_1 (or_1_out, and_1_out, \秒钟_out_13 );
  \电子钟整点报时电路  \u_电子钟整点报时电路_1  (.out_4(out_8), .in_1(24'h5950), .in_2(multiplexer_1_out), .in_3(clock_1_out));
  and and_2 (and_2_out, adj0, adj1, cpd);
  Multiplexer #(.select(1), .width(24), .disabled("Z"), .enable("false")) multiplexer_1 (
    .in0({24{1'b0}}), .in1(24'h5950), .out(multiplexer_1_out), .sel(and_3_out));
  not not_1 (not_1_out, adj1);
  \六十进制计数器  \u_分钟  (
    .cir(clr), .cpu(or_1_out), .cpd(and_2_out), .adj(adj0), .out_9(out_23), .out_10(out_24), .out_11(out_25),
    .out_12(out_26), .out_5(out_19), .out_6(out_20), .out_7(out_21), .out_8(out_22), .out_13(\分钟_out_13 ));
  and and_3 (and_3_out, out_12, out_14, and_4_out, and_5_out);
  and and_4 (and_4_out, out_20, out_22);
  and and_5 (and_5_out, out_23, out_26);
  or or_2 (or_2_out, and_6_out, \分钟_out_13 );
  and and_6 (and_6_out, adj0, not_1_out, cpu);
  and and_7 (and_7_out, adj0, not_1_out, cpd);
  \十二进制计数器或二十四进制的计数器电路  \u_十二进制计数器或二十四进制的计数器电路_1  (
    .in_1(set), .cir(clr), .cpu(or_2_out), .cpd(and_7_out), .adj(adj0), .out_10(out_33), .out_11(out_34),
    .out_12(out_35), .out_13(out_36), .out_6(out_29), .out_7(out_30), .out_8(out_31), .out_9(out_32),
    .out_14(\十二进制计数器或二十四进制的计数器电路_1_out_14 ));
  or or_3 (or_3_out, out_33, out_34, out_35);
  and and_8 (and_8_out, or_3_out, out_32, set);
  D_Flip_Flop #(.trigger("rising"), .Pre_Clr_Positions("ABOVE_BELOW"), .NegatePresetClear("false"), .enable("false"), .NewFFLayout("true")) d_ff_1 (
    .clk(or_4_out), .D(d_ff_1_qn), .Q(d_ff_1_q), .Qn(d_ff_1_qn));  // open: preset, reset
  or or_4 (or_4_out, \十二进制计数器或二十四进制的计数器电路_1_out_14 , clr);
  \上下午文字显示的电路  \u_上下午文字显示的电路_1  (
    .in_1(not_2_out), .out_3(out_9), .out_4(out_10), .out_5(out_27), .out_6(out_28), .out_7(out_37),
    .in_2(or_6_out));
  or or_5 (or_5_out, and_8_out, out_31);
  or or_6 (or_6_out, or_5_out, d_ff_1_q);
  not not_2 (not_2_out, clr);
endmodule

module \多功能数字钟测试电路  (
  input  in_1,
  input  in_2,
  input  in_3,
  input  in_4
);

  wire button_1_out, button_2_out, clock_1_out, \多功能数字钟_1_out_8 , \多功能数字钟_1_out_38 ;
  wire [3:0] \多功能数字钟_1_out_14 , \多功能数字钟_1_out_18 , \多功能数字钟_1_out_22 , \多功能数字钟_1_out_26 , \多功能数字钟_1_out_32 ,
       \多功能数字钟_1_out_36 ;
  wire [6:0] \多功能数字钟_1_out_9 , \多功能数字钟_1_out_10 , \多功能数字钟_1_out_27 , \多功能数字钟_1_out_28 , \多功能数字钟_1_out_37 ;

  DotMatrix #(.inputtype("column"), .matrixcols(5), .matrixrows(7), .persist(0), .dotshape("square")) dotmatrix_1 (
    .col0(\多功能数字钟_1_out_9 ), .col1(\多功能数字钟_1_out_10 ), .col2(\多功能数字钟_1_out_27 ), .col3(\多功能数字钟_1_out_28 ),
    .col4(\多功能数字钟_1_out_37 ));
  Clock #(.highDuration(1), .lowDuration(1)) clock_1 (.out(clock_1_out));
  Hex_Digit_Display hex_digit_display_1 (.value(\多功能数字钟_1_out_36 ));  // open: dp
  Hex_Digit_Display hex_digit_display_2 (.value(\多功能数字钟_1_out_32 ));  // open: dp
  Button button_1 (.out(button_1_out));
  Hex_Digit_Display hex_digit_display_3 (.value(\多功能数字钟_1_out_22 ));  // open: dp
  \多功能数字钟  \u_多功能数字钟_1  (
    .adj0(in_1), .adj1(in_2), .cpd(button_2_out), .cpu(button_1_out), .out_9(\多功能数字钟_1_out_9 ),
    .out_10(\多功能数字钟_1_out_10 ), .out_27(\多功能数字钟_1_out_27 ), .out_28(\多功能数字钟_1_out_28 ),
    .out_37(\多功能数字钟_1_out_37 ), .set(in_3), .clr(in_4), .out_11(\多功能数字钟_1_out_14 [3]),
    .out_12(\多功能数字钟_1_out_14 [2]), .out_13(\多功能数字钟_1_out_14 [1]), .out_14(\多功能数字钟_1_out_14 [0]),
    .out_15(\多功能数字钟_1_out_18 [3]), .out_16(\多功能数字钟_1_out_18 [2]), .out_17(\多功能数字钟_1_out_18 [1]),
    .out_18(\多功能数字钟_1_out_18 [0]), .out_19(\多功能数字钟_1_out_22 [3]), .out_20(\多功能数字钟_1_out_22 [2]),
    .out_21(\多功能数字钟_1_out_22 [1]), .out_22(\多功能数字钟_1_out_22 [0]), .out_23(\多功能数字钟_1_out_26 [3]),
    .out_24(\多功能数字钟_1_out_26 [2]), .out_25(\多功能数字钟_1_out_26 [1]), .out_26(\多功能数字钟_1_out_26 [0]),
    .out_29(\多功能数字钟_1_out_32 [3]), .out_30(\多功能数字钟_1_out_32 [2]), .out_31(\多功能数字钟_1_out_32 [1]),
    .out_32(\多功能数字钟_1_out_32 [0]), .out_33(\多功能数字钟_1_out_36 [3]), .out_34(\多功能数字钟_1_out_36 [2]),
    .out_35(\多功能数字钟_1_out_36 [1]), .out_36(\多功能数字钟_1_out_36 [0]), .CP(clock_1_out), .out_8(\多功能数字钟_1_out_8 ),
    .out_38(\多功能数字钟_1_out_38 ));
  Button button_2 (.out(button_2_out));
  Hex_Digit_Display hex_digit_display_4 (.value(\多功能数字钟_1_out_26 ));  // open: dp
  Hex_Digit_Display hex_digit_display_5 (.value(\多功能数字钟_1_out_14 ));  // open: dp
  Hex_Digit_Display hex_digit_display_6 (.value(\多功能数字钟_1_out_18 ));  // open: dp
  LED #(.active("true")) led_1 (.in(\多功能数字钟_1_out_38 ));
  LED #(.active("true")) led_2 (.in(\多功能数字钟_1_out_8 ));
endmodule

module \闹钟  (
  input  in_1,
  input  [3:0] in_2,
  input  [3:0] in_3,
  input  [3:0] in_4,
  input  [3:0] in_5,
  input  [3:0] in_6,
  input  [3:0] in_7,
  input  CP,
  input  set,
  input  clr,
  input  adj0,
  input  adj1,
  input  cpd,
  input  cpu,
  output out_15,
  output out_16,
  output out_17,
  output out_18,
  output out_19,
  output out_20,
  output out_21,
  output out_22,
  output out_23,
  output out_24,
  output out_25,
  output out_26,
  output out_27,
  output out_28,
  output out_29,
  output out_30,
  output out_31,
  output out_32,
  output out_33,
  output out_34,
  output out_35,
  output out_36,
  output out_37,
  output out_38,
  output out_39
);

  wire and_1_out, and_2_out, and_4_out, and_5_out, clock_1_out, not_1_out, or_1_out, or_2_out, \分钟_out_13 ,
       \十二进制计数器或二十四进制的计数器电路_1_out_14 , \电子钟整点报时电路_1_out_4 , \秒脉冲产生电路_1_out_2 , \秒钟_out_13 ;

  Clock #(.highDuration(1), .lowDuration(1)) clock_1 (.out(clock_1_out));
  \秒脉冲产生电路  \u_秒脉冲产生电路_1  (.in_1(CP), .out_2(\秒脉冲产生电路_1_out_2 ));
  \六十进制计数器  \u_秒钟  (
    .cir(clr), .cpu(\秒脉冲产生电路_1_out_2 ), .cpd(1'b0), .adj(adj0), .out_9(out_20), .out_10(out_21),
    .out_11(out_22), .out_12(out_23), .out_5(out_16), .out_6(out_17), .out_7(out_18), .out_8(out_19),
    .out_13(\秒钟_out_13 ));
  and and_1 (and_1_out, adj0, adj1, cpu);
  or or_1 (or_1_out, and_1_out, \秒钟_out_13 );
  \电子钟整点报时电路  \u_电子钟整点报时电路_1  (
    .out_4(\电子钟整点报时电路_1_out_4 ), .in_1({in_7, in_6, in_5, in_4, in_3, in_2}),
    .in_2({out_36, out_37, out_38, out_39, out_32, out_33, out_34, out_35, out_28, out_29, out_30, out_31, out_24, out_25, out_26, out_27, 4'b0000, out_16, out_17, out_18, out_19}),
    .in_3(clock_1_out));
  and and_2 (and_2_out, adj0, adj1, cpd);
  not not_1 (not_1_out, adj1);
  \六十进制计数器  \u_分钟  (
    .cir(clr), .cpu(or_1_out), .cpd(and_2_out), .adj(adj0), .out_9(out_28), .out_10(out_29), .out_11(out_30),
    .out_12(out_31), .out_5(out_24), .out_6(out_25), .out_7(out_26), .out_8(out_27), .out_13(\分钟_out_13 ));
  and and_3 (out_15, \电子钟整点报时电路_1_out_4 , in_1);
  or or_2 (or_2_out, and_4_out, \分钟_out_13 );
  and and_4 (and_4_out, adj0, not_1_out, cpu);
  and and_5 (and_5_out, adj0, not_1_out, cpd);
  LED #(.active("true")) led_1 (.in(\十二进制计数器或二十四进制的计数器电路_1_out_14 ));
  \十二进制计数器或二十四进制的计数器电路  \u_十二进制计数器或二十四进制的计数器电路_1  (
    .in_1(set), .cir(clr), .cpu(or_2_out), .cpd(and_5_out), .adj(adj0), .out_10(out_36), .out_11(out_37),
    .out_12(out_38), .out_13(out_39), .out_6(out_32), .out_7(out_33), .out_8(out_34), .out_9(out_35),
    .out_14(\十二进制计数器或二十四进制的计数器电路_1_out_14 ));
endmodule

module \闹钟测试  (
  input  [3:0] in_1,
  input  [3:0] in_2,
  input  [3:0] in_3,
  input  [3:0] in_4,
  input  [3:0] in_5,
  input  [3:0] in_6,
  input  in_7,
  input  in_8,
  input  in_9,
  input  in_10,
  input  in_11
);

  wire button_1_out, button_2_out, button_3_out, clock_1_out, \闹钟_1_out_15 ;
  wire [3:0] \闹钟_1_out_19 , \闹钟_1_out_23 , \闹钟_1_out_27 , \闹钟_1_out_31 , \闹钟_1_out_35 , \闹钟_1_out_39 ;

  Hex_Digit_Display hex_digit_display_1 (.value(\闹钟_1_out_35 ));  // open: dp
  Clock #(.highDuration(1), .lowDuration(1)) clock_1 (.out(clock_1_out));
  Hex_Digit_Display hex_digit_display_2 (.value(\闹钟_1_out_39 ));  // open: dp
  Button button_1 (.out(button_1_out));
  Hex_Digit_Display hex_digit_display_3 (.value(\闹钟_1_out_31 ));  // open: dp
  Hex_Digit_Display hex_digit_display_4 (.value(\闹钟_1_out_27 ));  // open: dp
  Button button_2 (.out(button_2_out));
  Button button_3 (.out(button_3_out));
  Hex_Digit_Display hex_digit_display_5 (.value(\闹钟_1_out_19 ));  // open: dp
  \闹钟  \u_闹钟_1  (
    .in_2(in_5), .in_3(in_6), .in_4(in_3), .in_5(in_4), .in_6(in_1), .in_7(in_2), .CP(clock_1_out),
    .adj0(in_7), .adj1(in_8), .cpd(button_2_out), .cpu(button_1_out), .set(in_10), .clr(in_11),
    .out_16(\闹钟_1_out_19 [3]), .out_17(\闹钟_1_out_19 [2]), .out_18(\闹钟_1_out_19 [1]),
    .out_19(\闹钟_1_out_19 [0]), .out_20(\闹钟_1_out_23 [3]), .out_21(\闹钟_1_out_23 [2]),
    .out_22(\闹钟_1_out_23 [1]), .out_23(\闹钟_1_out_23 [0]), .out_24(\闹钟_1_out_27 [3]),
    .out_25(\闹钟_1_out_27 [2]), .out_26(\闹钟_1_out_27 [1]), .out_27(\闹钟_1_out_27 [0]),
    .out_28(\闹钟_1_out_31 [3]), .out_29(\闹钟_1_out_31 [2]), .out_30(\闹钟_1_out_31 [1]),
    .out_31(\闹钟_1_out_31 [0]), .out_32(\闹钟_1_out_35 [3]), .out_33(\闹钟_1_out_35 [2]),
    .out_34(\闹钟_1_out_35 [1]), .out_35(\闹钟_1_out_35 [0]), .out_36(\闹钟_1_out_39 [3]),
    .out_37(\闹钟_1_out_39 [2]), .out_38(\闹钟_1_out_39 [1]), .out_39(\闹钟_1_out_39 [0]), .in_1(in_9),
    .out_15(\闹钟_1_out_15 ));
  Hex_Digit_Display hex_digit_display_6 (.value(\闹钟_1_out_23 ));  // open: dp
  LED #(.active("true")) led_1 (.in(\闹钟_1_out_15 ));
endmodule
