// Logisim project 实验4-CS2009-U202012656-张锦程.circ as structural Verilog: 5 circuits, main circuit 四位除法器
module \四位除法器  (
  input  [3:0] n2,
  input  [3:0] d,
  output [3:0] out_3,
  output [3:0] out_4
);

  wire comparator_1_gt, comparator_2_gt, comparator_3_gt, comparator_4_gt;
  wire [3:0] multiplexer_1_out, multiplexer_2_out, multiplexer_3_out, multiplexer_4_out, multiplexer_5_out,
       multiplexer_6_out, or_1_out, or_2_out, or_3_out, or_4_out, shifter_1_out, shifter_4_out,
       subtractor_1_out, subtractor_2_out, subtractor_3_out, subtractor_4_out;
  wire [7:0] shifter_2_out, shifter_3_out;
  wire [7:4] shifter_1_out_2, shifter_4_out_2;

  assign or_1_out = 4'b0001 | shifter_1_out;  // OR_Gate or_1, 4 bits wide
  Shifter #(.width(8), .shift("ll")) shifter_1 (
    .in({4'b0000, n2}), .\dist (3'b001), .out({shifter_1_out_2, shifter_1_out}));
  Multiplexer #(.select(1), .width(4), .disabled("Z"), .enable("false")) multiplexer_1 (
    .in0(or_1_out), .in1(shifter_1_out), .out(multiplexer_1_out), .sel(comparator_1_gt));
  Comparator #(.width(4), .mode("unsigned")) comparator_1 (
    .a(d), .b(shifter_1_out_2), .gt(comparator_1_gt));  // open: eq, lt
  Subtractor #(.width(4)) subtractor_1 (.a(shifter_1_out_2), .b(d), .out(subtractor_1_out));  // open: bin, bout
  Multiplexer #(.select(1), .width(4), .disabled("Z"), .enable("false")) multiplexer_2 (
    .in0(subtractor_1_out), .in1(shifter_1_out_2), .out(multiplexer_2_out), .sel(comparator_1_gt));
  assign or_2_out = 4'b0001 | shifter_2_out[3:0];  // OR_Gate or_2, 4 bits wide
  Shifter #(.width(8), .shift("ll")) shifter_2 (
    .in({multiplexer_2_out, multiplexer_1_out}), .\dist (3'b001), .out(shifter_2_out));
  Subtractor #(.width(4)) subtractor_2 (.a(shifter_2_out[7:4]), .b(d), .out(subtractor_2_out));  // open: bin, bout
  Multiplexer #(.select(1), .width(4), .disabled("Z"), .enable("false")) multiplexer_3 (
    .in0(or_2_out), .in1(shifter_2_out[3:0]), .out(multiplexer_3_out), .sel(comparator_2_gt));
  Comparator #(.width(4), .mode("unsigned")) comparator_2 (
    .a(d), .b(shifter_2_out[7:4]), .gt(comparator_2_gt));  // open: eq, lt
  Multiplexer #(.select(1), .width(4), .disabled("Z"), .enable("false")) multiplexer_4 (
    .in0(subtractor_2_out), .in1(shifter_2_out[7:4]), .out(multiplexer_4_out), .sel(comparator_2_gt));
  assign or_3_out = 4'b0001 | shifter_3_out[3:0];  // OR_Gate or_3, 4 bits wide
  Shifter #(.width(8), .shift("ll")) shifter_3 (
    .in({multiplexer_4_out, multiplexer_3_out}), .\dist (3'b001), .out(shifter_3_out));
  Multiplexer #(.select(1), .width(4), .disabled("Z"), .enable("false")) multiplexer_5 (
    .in0(or_3_out), .in1(shifter_3_out[3:0]), .out(multiplexer_5_out), .sel(comparator_3_gt));
  Comparator #(.width(4), .mode("unsigned")) comparator_3 (
    .a(d), .b(shifter_3_out[7:4]), .gt(comparator_3_gt));  // open: eq, lt
  Subtractor #(.width(4)) subtractor_3 (.a(shifter_3_out[7:4]), .b(d), .out(subtractor_3_out));  // open: bin, bout
  Multiplexer #(.select(1), .width(4), .disabled("Z"), .enable("false")) multiplexer_6 (
    .in0(subtractor_3_out), .in1(shifter_3_out[7:4]), .out(multiplexer_6_out), .sel(comparator_3_gt));
  assign or_4_out = 4'b0001 | shifter_4_out;  // OR_Gate or_4, 4 bits wide
  Shifter #(.width(8), .shift("ll")) shifter_4 (
    .in({multiplexer_6_out, multiplexer_5_out}), .\dist (3'b001), .out({shifter_4_out_2, shifter_4_out}));
  Multiplexer #(.select(1), .width(4), .disabled("Z"), .enable("false")) multiplexer_7 (
    .in0(or_4_out), .in1(shifter_4_out), .out(out_3), .sel(comparator_4_gt));
  Comparator #(.width(4), .mode("unsigned")) comparator_4 (
    .a(d), .b(shifter_4_out_2), .gt(comparator_4_gt));  // open: eq, lt
  Subtractor #(.width(4)) subtractor_4 (.a(shifter_4_out_2), .b(d), .out(subtractor_4_out));  // open: bin, bout
  Multiplexer #(.select(1), .width(4), .disabled("Z"), .enable("false")) multiplexer_8 (
    .in0(subtractor_4_out), .in1(shifter_4_out_2), .out(out_4), .sel(comparator_4_gt));

  // Notes on the sheet:
  //   n1
endmodule

module \四位除法器测试电路  (
  input  [3:0] in_1,
  input  [3:0] in_2,
  output [3:0] out_3,
  output [3:0] out_4
);

  \四位除法器  \u_四位除法器_1  (.n2(in_1), .d(in_2), .out_3(out_3), .out_4(out_4));
endmodule

module _32_div1 (
  input  [31:0] in_1,
  input  [31:0] in_2,
  input  [31:0] in_3,
  output [31:0] out_4,
  output [31:0] out_5
);

  wire comparator_1_gt;
  wire [31:0] or_1_out, or_2_out, shifter_1_out, shifter_2_out, shifter_3_out, subtractor_1_out;

  Shifter #(.width(32), .shift("ll")) shifter_1 (.in(in_2), .\dist (5'b00001), .out(shifter_1_out));
  Shifter #(.width(32), .shift("lr")) shifter_2 (.in(in_3), .\dist ({5{1'b1}}), .out(shifter_2_out));
  assign or_1_out = shifter_1_out | shifter_2_out;  // OR_Gate or_1, 32 bits wide
  Shifter #(.width(32), .shift("ll")) shifter_3 (.in(in_3), .\dist (5'b00001), .out(shifter_3_out));
  Subtractor #(.width(32)) subtractor_1 (.a(or_1_out), .b(in_1), .out(subtractor_1_out));  // open: bin, bout
  Multiplexer #(.select(1), .width(32), .disabled("Z"), .enable("false")) multiplexer_1 (
    .in0(or_2_out), .in1(shifter_3_out), .out(out_5), .sel(comparator_1_gt));
  Comparator #(.width(32), .mode("unsigned")) comparator_1 (
    .a(in_1), .b(or_1_out), .gt(comparator_1_gt));  // open: eq, lt
  Multiplexer #(.select(1), .width(32), .disabled("Z"), .enable("false")) multiplexer_2 (
    .in0(subtractor_1_out), .in1(or_1_out), .out(out_4), .sel(comparator_1_gt));
  assign or_2_out = 32'h1 | shifter_3_out;  // OR_Gate or_2, 32 bits wide

  // Notes on the sheet:
  //   cur_rem
  //   cur_quot
  //   d
  //   rem
  //   quot
  //   rem
  //   next_rem
  //   next_quot
endmodule

module \_32位除法器  (
  input  [31:0] d,
  input  [31:0] n2,
  output [31:0] rem,
  output [31:0] quot
);

  wire [31:0] n32_div1_1_out_4, n32_div1_1_out_5, n32_div1_3_out_4, n32_div1_3_out_5, n32_div1_4_out_4,
       n32_div1_4_out_5, n32_div1_5_out_4, n32_div1_5_out_5, n32_div1_6_out_4, n32_div1_6_out_5,
       n32_div1_7_out_4, n32_div1_7_out_5, n32_div1_8_out_4, n32_div1_8_out_5, n32_div1_9_out_4,
       n32_div1_9_out_5, n32_div1_10_out_4, n32_div1_10_out_5, n32_div1_11_out_4, n32_div1_11_out_5,
       n32_div1_12_out_4, n32_div1_12_out_5, n32_div1_13_out_4, n32_div1_13_out_5, n32_div1_14_out_4,
       n32_div1_14_out_5, n32_div1_15_out_4, n32_div1_15_out_5, n32_div1_16_out_4, n32_div1_16_out_5,
       n32_div1_17_out_4, n32_div1_17_out_5, n32_div1_18_out_4, n32_div1_18_out_5, n32_div1_19_out_4,
       n32_div1_19_out_5, n32_div1_20_out_4, n32_div1_20_out_5, n32_div1_21_out_4, n32_div1_21_out_5,
       n32_div1_22_out_4, n32_div1_22_out_5, n32_div1_23_out_4, n32_div1_23_out_5, n32_div1_24_out_4,
       n32_div1_24_out_5, n32_div1_25_out_4, n32_div1_25_out_5, n32_div1_26_out_4, n32_div1_26_out_5,
       n32_div1_27_out_4, n32_div1_27_out_5, n32_div1_28_out_4, n32_div1_28_out_5, n32_div1_29_out_4,
       n32_div1_29_out_5, n32_div1_30_out_4, n32_div1_30_out_5, n32_div1_31_out_4, n32_div1_31_out_5,
       n32_div1_32_out_4, n32_div1_32_out_5;

  _32_div1 u_32_div1_1 (
    .in_1(d), .in_2(n32_div1_4_out_4), .in_3(n32_div1_4_out_5), .out_4(n32_div1_1_out_4),
    .out_5(n32_div1_1_out_5));
  _32_div1 u_32_div1_2 (.in_1(d), .in_2(n32_div1_6_out_4), .in_3(n32_div1_6_out_5), .out_4(rem), .out_5(quot));
  _32_div1 u_32_div1_3 (.in_1(d), .in_2({32{1'b0}}), .in_3(n2), .out_4(n32_div1_3_out_4), .out_5(n32_div1_3_out_5));
  _32_div1 u_32_div1_4 (
    .in_1(d), .in_2(n32_div1_9_out_4), .in_3(n32_div1_9_out_5), .out_4(n32_div1_4_out_4),
    .out_5(n32_div1_4_out_5));
  _32_div1 u_32_div1_5 (
    .in_1(d), .in_2(n32_div1_1_out_4), .in_3(n32_div1_1_out_5), .out_4(n32_div1_5_out_4),
    .out_5(n32_div1_5_out_5));
  _32_div1 u_32_div1_6 (
    .in_1(d), .in_2(n32_div1_10_out_4), .in_3(n32_div1_10_out_5), .out_4(n32_div1_6_out_4),
    .out_5(n32_div1_6_out_5));
  _32_div1 u_32_div1_7 (
    .in_1(d), .in_2(n32_div1_3_out_4), .in_3(n32_div1_3_out_5), .out_4(n32_div1_7_out_4),
    .out_5(n32_div1_7_out_5));
  _32_div1 u_32_div1_8 (
    .in_1(d), .in_2(n32_div1_5_out_4), .in_3(n32_div1_5_out_5), .out_4(n32_div1_8_out_4),
    .out_5(n32_div1_8_out_5));
  _32_div1 u_32_div1_9 (
    .in_1(d), .in_2(n32_div1_12_out_4), .in_3(n32_div1_12_out_5), .out_4(n32_div1_9_out_4),
    .out_5(n32_div1_9_out_5));
  _32_div1 u_32_div1_10 (
    .in_1(d), .in_2(n32_div1_14_out_4), .in_3(n32_div1_14_out_5), .out_4(n32_div1_10_out_4),
    .out_5(n32_div1_10_out_5));
  _32_div1 u_32_div1_11 (
    .in_1(d), .in_2(n32_div1_7_out_4), .in_3(n32_div1_7_out_5), .out_4(n32_div1_11_out_4),
    .out_5(n32_div1_11_out_5));
  _32_div1 u_32_div1_12 (
    .in_1(d), .in_2(n32_div1_17_out_4), .in_3(n32_div1_17_out_5), .out_4(n32_div1_12_out_4),
    .out_5(n32_div1_12_out_5));
  _32_div1 u_32_div1_13 (
    .in_1(d), .in_2(n32_div1_8_out_4), .in_3(n32_div1_8_out_5), .out_4(n32_div1_13_out_4),
    .out_5(n32_div1_13_out_5));
  _32_div1 u_32_div1_14 (
    .in_1(d), .in_2(n32_div1_18_out_4), .in_3(n32_div1_18_out_5), .out_4(n32_div1_14_out_4),
    .out_5(n32_div1_14_out_5));
  _32_div1 u_32_div1_15 (
    .in_1(d), .in_2(n32_div1_11_out_4), .in_3(n32_div1_11_out_5), .out_4(n32_div1_15_out_4),
    .out_5(n32_div1_15_out_5));
  _32_div1 u_32_div1_16 (
    .in_1(d), .in_2(n32_div1_13_out_4), .in_3(n32_div1_13_out_5), .out_4(n32_div1_16_out_4),
    .out_5(n32_div1_16_out_5));
  _32_div1 u_32_div1_17 (
    .in_1(d), .in_2(n32_div1_20_out_4), .in_3(n32_div1_20_out_5), .out_4(n32_div1_17_out_4),
    .out_5(n32_div1_17_out_5));
  _32_div1 u_32_div1_18 (
    .in_1(d), .in_2(n32_div1_22_out_4), .in_3(n32_div1_22_out_5), .out_4(n32_div1_18_out_4),
    .out_5(n32_div1_18_out_5));
  _32_div1 u_32_div1_19 (
    .in_1(d), .in_2(n32_div1_15_out_4), .in_3(n32_div1_15_out_5), .out_4(n32_div1_19_out_4),
    .out_5(n32_div1_19_out_5));
  _32_div1 u_32_div1_20 (
    .in_1(d), .in_2(n32_div1_25_out_4), .in_3(n32_div1_25_out_5), .out_4(n32_div1_20_out_4),
    .out_5(n32_div1_20_out_5));
  _32_div1 u_32_div1_21 (
    .in_1(d), .in_2(n32_div1_16_out_4), .in_3(n32_div1_16_out_5), .out_4(n32_div1_21_out_4),
    .out_5(n32_div1_21_out_5));
  _32_div1 u_32_div1_22 (
    .in_1(d), .in_2(n32_div1_26_out_4), .in_3(n32_div1_26_out_5), .out_4(n32_div1_22_out_4),
    .out_5(n32_div1_22_out_5));
  _32_div1 u_32_div1_23 (
    .in_1(d), .in_2(n32_div1_19_out_4), .in_3(n32_div1_19_out_5), .out_4(n32_div1_23_out_4),
    .out_5(n32_div1_23_out_5));
  _32_div1 u_32_div1_24 (
    .in_1(d), .in_2(n32_div1_21_out_4), .in_3(n32_div1_21_out_5), .out_4(n32_div1_24_out_4),
    .out_5(n32_div1_24_out_5));
  _32_div1 u_32_div1_25 (
    .in_1(d), .in_2(n32_div1_28_out_4), .in_3(n32_div1_28_out_5), .out_4(n32_div1_25_out_4),
    .out_5(n32_div1_25_out_5));
  _32_div1 u_32_div1_26 (
    .in_1(d), .in_2(n32_div1_30_out_4), .in_3(n32_div1_30_out_5), .out_4(n32_div1_26_out_4),
    .out_5(n32_div1_26_out_5));
  _32_div1 u_32_div1_27 (
    .in_1(d), .in_2(n32_div1_23_out_4), .in_3(n32_div1_23_out_5), .out_4(n32_div1_27_out_4),
    .out_5(n32_div1_27_out_5));
  _32_div1 u_32_div1_28 (
    .in_1(d), .in_2(n32_div1_31_out_4), .in_3(n32_div1_31_out_5), .out_4(n32_div1_28_out_4),
    .out_5(n32_div1_28_out_5));
  _32_div1 u_32_div1_29 (
    .in_1(d), .in_2(n32_div1_24_out_4), .in_3(n32_div1_24_out_5), .out_4(n32_div1_29_out_4),
    .out_5(n32_div1_29_out_5));
  _32_div1 u_32_div1_30 (
    .in_1(d), .in_2(n32_div1_32_out_4), .in_3(n32_div1_32_out_5), .out_4(n32_div1_30_out_4),
    .out_5(n32_div1_30_out_5));
  _32_div1 u_32_div1_31 (
    .in_1(d), .in_2(n32_div1_27_out_4), .in_3(n32_div1_27_out_5), .out_4(n32_div1_31_out_4),
    .out_5(n32_div1_31_out_5));
  _32_div1 u_32_div1_32 (
    .in_1(d), .in_2(n32_div1_29_out_4), .in_3(n32_div1_29_out_5), .out_4(n32_div1_32_out_4),
    .out_5(n32_div1_32_out_5));

  // Notes on the sheet:
  //   n1
endmodule

module \_32位除法器测试电路  (
  input  [31:0] in_1,
  input  [31:0] in_2,
  output [31:0] out_3,
  output [31:0] out_4
);

  // Probe on in_1
  // Probe on in_2
  // Probe on out_3
  \_32位除法器  \u_32位除法器_1  (.rem(out_4), .quot(out_3), .n2(in_1), .d(in_2));
  // Probe on out_4
endmodule
